# Fritzing sketch Smart_Key_Sketch (saved by Fritzing 0.9.3b)
breadboards: 1

parts:
  U2 = NodeMCU V1.0
  Part1 = Arduino Mega 2560 (Rev3)
  Keypad4x2 = Keypad Membran 4x4
  J1 = Piezo Speaker
  Part2 = sensor_biometrico
  VCC1 = Battery block 9V
  Mod1 = KY-019 5V Relay Module [package="Breakout board"]
  J2 = Basic Servo
  L1 = Solenoid
  open_door = Round Pushbutton
  knock_check = Round Pushbutton
  close_door = Round Pushbutton
  bell = Round Pushbutton
  FC-1 = Sound Sensor
  ESP32_-_Back1 = ESP32 - CAM
  FTDI_USB_UART1 = CP2102 USB UART [part_number="USB UART"]

nets:
  N1: U2.D0, knock_check.leg1
  N2: U2.D1, Mod1.S
  N3: U2.D2, J1.pin2
  N4: U2.D3, bell.leg1
  N5: U2.D4, J2.pulse
  GND: U2.GND, J1.pin1, Part2.GND, Mod1.-, J2.gnd, open_door.leg0, knock_check.leg0, close_door.leg0, bell.leg0, FC-1.GND
  N6: U2.D5, open_door.leg1
  N7: U2.D6, close_door.leg1
  N8: U2.D7, Part2.TX
  N9: U2.D8, Part2.RX
  VCC: U2.3V3, Part2.VCC, Mod1.+, J2.vcc, FC-1.VCC
  N10: U2.A0, FC-1.OUT
  N11: Part1.D9_PWM, Keypad4x2.Pin1
  N12: Part1.D8_PWM, Keypad4x2.Pin2
  N13: Part1.D2_PWM, Keypad4x2.Pin8
  N14: Part1.D3_PWM, Keypad4x2.Pin7
  N15: Part1.D4_PWM, Keypad4x2.Pin6
  N16: Part1.D5_PWM, Keypad4x2.Pin5
  N17: Part1.D6_PWM, Keypad4x2.Pin4
  N18: Part1.D7_PWM, Keypad4x2.Pin3
  N19: VCC1.-, L1.pin1
  N20: VCC1.+, Mod1.Common
  N21: Mod1.NO, L1.pin2
  5V: ESP32_-_Back1.5V, FTDI_USB_UART1.+5V
  N22: ESP32_-_Back1.GPIO0, FTDI_USB_UART1.DTR
  N23: ESP32_-_Back1.GPIO3_/_RX, FTDI_USB_UART1.TXO
  N24: ESP32_-_Back1.GPIO1_/_TX, FTDI_USB_UART1.RXI
  GND_2: ESP32_-_Back1.GND, FTDI_USB_UART1.GND

notes:
  press rst and connect IO0 of esp32 cam to ftdi DTR only for uploading the code, whenever ..... appear disconnect it and release the rst button

custom parts:
  NodeMCU V1.0: ESP8266 based NodeMCU
  Keypad Membran 4x4: Membrane Keypad 4x4 Matrix
  sensor_biometrico: Adafruit Optical Fingerprint Sensor
  KY-019 5V Relay Module: KY-019 5V Relay module, used to control AC circuits. (Special thanks to vanepp for fixing the PCB holes and other errors)
  ESP32 - CAM: The ESP32-CAM has a very competitive small-size camera module that can operate independently as a minimum system with a footprint of only 27*40.5*4.5mm and a deep sleep current of up to 6mA.
  CP2102 USB UART: CP2102 USB UART FTDI
